// Logisim project Calculator.circ as structural Verilog: 6 circuits, main circuit main
module main (
  input  [4:0] in_1,
  input  [4:0] in_2,
  input  [1:0] in_3,
  output [18:0] out_4
);

  wire [4:0] demultiplexer_1_out0, demultiplexer_1_out1, demultiplexer_1_out2, demultiplexer_1_out3;
  wire [18:0] adder_1_out_3, division_1_out_3, multiplier_1_out_3, subtractor_1_out_3;

  Demultiplexer #(.select(2), .width(5)) demultiplexer_1 (
    .out0(demultiplexer_1_out0), .out1(demultiplexer_1_out1), .out2(demultiplexer_1_out2),
    .out3(demultiplexer_1_out3), .in(in_1), .sel(in_3));  // open: en
  ADDER adder_1 (.in_1(demultiplexer_1_out0), .in_2(in_2), .out_3(adder_1_out_3));
  SUBTRACTOR subtractor_1 (.in_1(demultiplexer_1_out1), .in_2(in_2), .out_3(subtractor_1_out_3));
  MULTIPLIER multiplier_1 (.in_1(demultiplexer_1_out2), .in_2(in_2), .out_3(multiplier_1_out_3));
  DIVISION division_1 (.in_1(demultiplexer_1_out3), .in_2(in_2), .out_3(division_1_out_3));
  Multiplexer #(.select(2), .width(19)) multiplexer_1 (
    .in0(adder_1_out_3), .in1(subtractor_1_out_3), .in2(multiplier_1_out_3), .in3(division_1_out_3),
    .out(out_4), .sel(in_3));  // open: en
endmodule

module ADDER (
  input  [4:0] in_1,
  input  [4:0] in_2,
  output [18:0] out_3
);

  wire adder_1_cout;
  wire [4:0] adder_1_out;
  wire [18:0] bit_extender_1_out, carryin_1_out_2;

  Adder #(.width(5)) adder_1 (.a(in_1), .b(in_2), .out(adder_1_out), .cout(adder_1_cout));  // open: cin
  assign bit_extender_1_out = {{14{1'b0}}, adder_1_out};  // Bit_Extender bit_extender_1
  CarryIn carryin_1 (.in_1(adder_1_cout), .out_2(carryin_1_out_2));
  Adder #(.width(19)) adder_2 (.a(bit_extender_1_out), .b(carryin_1_out_2), .out(out_3));  // open: cin, cout
endmodule

module CarryIn (
  input  in_1,
  output [18:0] out_2
);

  wire [18:0] bit_extender_1_out;

  assign bit_extender_1_out = {{18{1'b0}}, in_1};  // Bit_Extender bit_extender_1
  Shifter #(.width(19)) shifter_1 (.in(bit_extender_1_out), .\dist (5'b10010), .out(out_2));
endmodule

module SUBTRACTOR (
  input  [4:0] in_1,
  input  [4:0] in_2,
  output [18:0] out_3
);

  wire subtractor_1_bout;
  wire [4:0] subtractor_1_out;
  wire [18:0] bit_extender_1_out, carryin_1_out_2;

  Subtractor #(.width(5)) subtractor_1 (
    .a(in_1), .b(in_2), .out(subtractor_1_out), .bout(subtractor_1_bout));  // open: bin
  assign bit_extender_1_out = {{14{1'b0}}, subtractor_1_out};  // Bit_Extender bit_extender_1
  CarryIn carryin_1 (.in_1(subtractor_1_bout), .out_2(carryin_1_out_2));
  Subtractor #(.width(19)) subtractor_2 (.a(bit_extender_1_out), .b(carryin_1_out_2), .out(out_3));  // open: bin, bout
endmodule

module MULTIPLIER (
  input  [4:0] in_1,
  input  [4:0] in_2,
  output [18:0] out_3
);

  wire [4:0] multiplier_1_cout, multiplier_1_out;
  wire [18:0] bit_extender_1_out, bit_extender_2_out, shifter_1_out;

  Multiplier #(.width(5)) multiplier_1 (
    .a(in_1), .b(in_2), .out(multiplier_1_out), .cout(multiplier_1_cout));  // open: cin
  assign bit_extender_1_out = {{14{1'b0}}, multiplier_1_out};  // Bit_Extender bit_extender_1
  assign bit_extender_2_out = {{14{1'b0}}, multiplier_1_cout};  // Bit_Extender bit_extender_2
  Shifter #(.width(19)) shifter_1 (.in(bit_extender_2_out), .\dist (5'b10010), .out(shifter_1_out));
  Adder #(.width(19)) adder_1 (.a(bit_extender_1_out), .b(shifter_1_out), .out(out_3));  // open: cin, cout
endmodule

module DIVISION (
  input  [4:0] in_1,
  input  [4:0] in_2,
  output [18:0] out_3
);

  wire [4:0] divider_1_out, divider_1_rem;
  wire [18:0] bit_extender_1_out, bit_extender_2_out, shifter_1_out;

  Divider #(.width(5)) divider_1 (.a(in_1), .b(in_2), .out(divider_1_out), .rem(divider_1_rem));  // open: upper
  assign bit_extender_1_out = {{14{1'b0}}, divider_1_out};  // Bit_Extender bit_extender_1
  assign bit_extender_2_out = {{14{1'b0}}, divider_1_rem};  // Bit_Extender bit_extender_2
  Shifter #(.width(19)) shifter_1 (.in(bit_extender_2_out), .\dist (5'b10010), .out(shifter_1_out));
  Adder #(.width(19)) adder_1 (.a(bit_extender_1_out), .b(shifter_1_out), .out(out_3));  // open: cin, cout
endmodule
