// Logisim project DisplayExample.circ as structural Verilog: 1 circuit, main circuit main
module main (
  input  [19:0] in_1
);

  wire [19:0] rom_1_data, rom_2_data, rom_3_data, rom_4_data, rom_5_data, rom_6_data, rom_7_data, rom_8_data,
       rom_9_data, rom_10_data, rom_11_data, rom_12_data, rom_13_data, rom_14_data, rom_15_data, rom_16_data,
       rom_17_data, rom_18_data, rom_20_data;

  ROM #(.addrWidth(20), .dataWidth(20)) rom_1 (.addr(in_1), .data(rom_1_data));  // open: sel
  ROM #(.addrWidth(20), .dataWidth(20)) rom_2 (.addr(in_1), .data(rom_2_data));  // open: sel
  ROM #(.addrWidth(20), .dataWidth(20)) rom_3 (.addr(in_1), .data(rom_3_data));  // open: sel
  ROM #(.addrWidth(20), .dataWidth(20)) rom_4 (.addr(in_1), .data(rom_4_data));  // open: sel
  ROM #(.addrWidth(20), .dataWidth(20)) rom_5 (.addr(in_1), .data(rom_5_data));  // open: sel
  ROM #(.addrWidth(20), .dataWidth(20)) rom_6 (.addr(in_1), .data(rom_6_data));  // open: sel
  ROM #(.addrWidth(20), .dataWidth(20)) rom_7 (.addr(in_1), .data(rom_7_data));  // open: sel
  ROM #(.addrWidth(20), .dataWidth(20)) rom_8 (.addr(in_1), .data(rom_8_data));  // open: sel
  ROM #(.addrWidth(20), .dataWidth(20)) rom_9 (.addr(in_1), .data(rom_9_data));  // open: sel
  ROM #(.addrWidth(20), .dataWidth(20)) rom_10 (.addr(in_1), .data(rom_10_data));  // open: sel
  ROM #(.addrWidth(20), .dataWidth(20)) rom_11 (.addr(in_1), .data(rom_11_data));  // open: sel
  ROM #(.addrWidth(20), .dataWidth(20)) rom_12 (.addr(in_1), .data(rom_12_data));  // open: sel
  ROM #(.addrWidth(20), .dataWidth(20)) rom_13 (.addr(in_1), .data(rom_13_data));  // open: sel
  ROM #(.addrWidth(20), .dataWidth(20)) rom_14 (.addr(in_1), .data(rom_14_data));  // open: sel
  ROM #(.addrWidth(20), .dataWidth(20)) rom_15 (.addr(in_1), .data(rom_15_data));  // open: sel
  ROM #(.addrWidth(20), .dataWidth(20)) rom_16 (.addr(in_1), .data(rom_16_data));  // open: sel
  ROM #(.addrWidth(20), .dataWidth(20)) rom_17 (.addr(in_1), .data(rom_17_data));  // open: sel
  ROM #(.addrWidth(20), .dataWidth(20)) rom_18 (.addr(in_1), .data(rom_18_data));  // open: sel
  ROM #(.addrWidth(20), .dataWidth(20)) rom_19 (.addr(in_1), .data(rom_18_data));  // open: sel
  ROM #(.addrWidth(20), .dataWidth(20)) rom_20 (.addr(in_1), .data(rom_20_data));  // open: sel
  DotMatrix #(.matrixcols(20), .matrixrows(20)) dotmatrix_1 (
    .col0(rom_1_data), .col1(rom_2_data), .col2(rom_3_data), .col3(rom_4_data), .col4(rom_5_data),
    .col5(rom_6_data), .col6(rom_7_data), .col7(rom_8_data), .col8(rom_9_data), .col9(rom_10_data),
    .col10(rom_11_data), .col11(rom_12_data), .col12(rom_13_data), .col13(rom_14_data), .col14(rom_15_data),
    .col15(rom_16_data), .col16(rom_17_data), .col17(rom_18_data), .col18(rom_18_data), .col19(rom_20_data));

  // Notes on the sheet:
  //   contents of rom_1 (hex, n*v repeats v):
  //   12 1 3 13*0 2
  //   contents of rom_2 (hex, n*v repeats v):
  //   1
endmodule
