// Logisim project DisplayTest.circ as structural Verilog: 2 circuits, main circuit main
module main (
  input  [3:0] in_1,
  input  [3:0] in_2,
  input  ADDRESS,
  input  [3:0] in_4,
  output [3:0] OUTPUT
);

  wire clock_1_out, not_1_out;
  wire [3:0] rom_1_data, rom_2_data, rom_3_data, rom_4_data;

  assign OUTPUT = ADDRESS ? in_1 : 4'bz;  // Controlled_Buffer controlled_buffer_1
  not not_1 (not_1_out, ADDRESS);
  Clock clock_1 (.out(clock_1_out));
  RAM #(.addrWidth(4), .dataWidth(4)) ram_1 (
    .addr(in_2), .data(OUTPUT), .clk(clock_1_out), .ld(not_1_out));  // open: sel, clr
  ROM #(.addrWidth(4), .dataWidth(4)) rom_1 (.addr(in_4), .data(rom_1_data));  // open: sel
  ROM #(.addrWidth(4), .dataWidth(4)) rom_2 (.addr(in_4), .data(rom_2_data));  // open: sel
  ROM #(.addrWidth(4), .dataWidth(4)) rom_3 (.addr(in_4), .data(rom_3_data));  // open: sel
  ROM #(.addrWidth(4), .dataWidth(4)) rom_4 (.addr(in_4), .data(rom_4_data));  // open: sel
  DotMatrix #(.matrixcols(4), .matrixrows(4)) dotmatrix_1 (
    .col0(rom_1_data), .col1(rom_2_data), .col2(rom_3_data), .col3(rom_4_data));

  // Notes on the sheet:
  //   contents of rom_1 (hex, n*v repeats v):
  //   a 9
  //   contents of rom_2 (hex, n*v repeats v):
  //   1 6
  //   contents of rom_3 (hex, n*v repeats v):
  //   1 6
  //   contents of rom_4 (hex, n*v repeats v):
  //   a 9
endmodule

module _4BIT_RAM (
  input  [3:0] in_1,
  input  [3:0] in_2,
  input  in_3,
  output [3:0] OUTPUT
);

  wire clock_1_out, not_1_out;

  Clock clock_1 (.out(clock_1_out));
  assign OUTPUT = in_3 ? in_1 : 4'bz;  // Controlled_Buffer controlled_buffer_1
  not not_1 (not_1_out, in_3);
  RAM #(.addrWidth(4), .dataWidth(4)) ram_1 (
    .addr(in_2), .data(OUTPUT), .clk(clock_1_out), .ld(not_1_out));  // open: sel, clr

  // Notes on the sheet:
  //   ADDRESS
endmodule
