// Logisim project KeyBoardTest.circ as structural Verilog: 2 circuits, main circuit main
module main (
  input  in_1,
  input  in_2,
  input  in_3,
  input  in_4,
  input  in_5,
  input  in_6,
  input  in_7,
  input  in_8,
  input  in_9,
  input  in_10,
  input  in_11,
  input  in_12,
  input  in_13,
  input  in_14,
  input  in_15,
  input  in_16,
  input  in_17,
  input  in_18,
  input  in_19,
  input  in_20,
  input  in_21,
  input  in_22,
  input  in_23,
  input  in_24,
  input  in_25,
  input  in_26
);

  wire rom_1_data, rom_2_data, rom_3_data, rom_4_data, rom_5_data, rom_6_data, rom_7_data, rom_8_data;
  wire [7:0] keyboard_1_out_27;

  KEYBOARD keyboard_1 (
    .in_1(in_1), .in_2(in_2), .in_3(in_3), .in_4(in_4), .in_5(in_5), .in_6(in_6), .in_7(in_7), .in_8(in_8),
    .in_9(in_9), .in_10(in_10), .in_11(in_11), .in_12(in_12), .in_13(in_13), .in_14(in_14), .in_15(in_15),
    .in_16(in_16), .in_17(in_17), .in_18(in_18), .in_19(in_19), .in_20(in_20), .in_21(in_21), .in_22(in_22),
    .in_23(in_23), .in_24(in_24), .in_25(in_25), .in_26(in_26), .out_27(keyboard_1_out_27));
  ROM #(.dataWidth(1)) rom_1 (.addr(keyboard_1_out_27), .data(rom_1_data));  // open: sel
  ROM #(.dataWidth(1)) rom_2 (.addr(keyboard_1_out_27), .data(rom_2_data));  // open: sel
  ROM #(.dataWidth(1)) rom_3 (.addr(keyboard_1_out_27), .data(rom_3_data));  // open: sel
  ROM #(.dataWidth(1)) rom_4 (.addr(keyboard_1_out_27), .data(rom_4_data));  // open: sel
  ROM #(.dataWidth(1)) rom_5 (.addr(keyboard_1_out_27), .data(rom_5_data));  // open: sel
  ROM #(.dataWidth(1)) rom_6 (.addr(keyboard_1_out_27), .data(rom_6_data));  // open: sel
  ROM #(.dataWidth(1)) rom_7 (.addr(keyboard_1_out_27), .data(rom_7_data));  // open: sel
  ROM #(.dataWidth(1)) rom_8 (.addr(keyboard_1_out_27), .data(rom_8_data));  // open: sel
  _7_Segment_Display u_7_segment_display_1 (
    .g(rom_4_data), .f(rom_3_data), .a(rom_2_data), .b(rom_1_data), .e(rom_5_data), .d(rom_6_data),
    .c(rom_7_data), .dp(rom_8_data));

  // Other names for the same wires on the sheet: A = in_1; B = in_2; C = in_3; D = in_4; E = in_5; F = in_6; G = in_7;
  //   H = in_8; I = in_9; J = in_10; K = in_11; L = in_12; M = in_13; N = in_14; O = in_15; P = in_16; Q = in_17;
  //   R = in_18; S = in_19; T = in_20; U = in_21; V = in_22; W = in_23; X = in_24; Y = in_25; Z = in_26

  // Notes on the sheet:
  //   contents of rom_1 (hex, n*v repeats v):
  //   0 1 1 0 1 0 0 0 1 0 1 5*0 1
  //   contents of rom_2 (hex, n*v repeats v):
  //   0 7*1 8*0 1
  //   contents of rom_3 (hex, n*v repeats v):
  //   0 9*1 0 0 1 0 0 0 1
  //   contents of rom_4 (hex, n*v repeats v):
  //   0 1 1 0 0 4*1
  //   contents of rom_5 (hex, n*v repeats v):
  //   0 9*1 0 0 1 0 0 0 1
  //   contents of rom_6 (hex, n*v repeats v):
  //   0 0 4*1 0 1 0 0 1 0 1 0 0 0 1
  //   contents of rom_7 (hex, n*v repeats v):
  //   0 1 1 0 1 0 0 1 1 0 1 5*0 1
endmodule

module KEYBOARD (
  input  in_1,
  input  in_2,
  input  in_3,
  input  in_4,
  input  in_5,
  input  in_6,
  input  in_7,
  input  in_8,
  input  in_9,
  input  in_10,
  input  in_11,
  input  in_12,
  input  in_13,
  input  in_14,
  input  in_15,
  input  in_16,
  input  in_17,
  input  in_18,
  input  in_19,
  input  in_20,
  input  in_21,
  input  in_22,
  input  in_23,
  input  in_24,
  input  in_25,
  input  in_26,
  output [7:0] out_27
);

  wire [4:0] priority_encoder_1_out;
  wire [7:0] bit_extender_1_out;

  Priority_Encoder #(.select(5), .disabled(0)) priority_encoder_1 (
    .in0(in_1), .in1(in_2), .in2(in_3), .in3(in_4), .in4(in_5), .in5(in_6), .in6(in_7), .in7(in_8),
    .in8(in_9), .in9(in_10), .in10(in_11), .in11(in_12), .in12(in_13), .in13(in_14), .in14(in_15),
    .in15(in_16), .in16(in_17), .in17(in_18), .in18(in_19), .in19(in_20), .in20(in_21), .in21(in_22),
    .in22(in_23), .in23(in_24), .in24(in_25), .in25(in_26), .out(priority_encoder_1_out), .en_in(1'b1));  // open: in26, in27, in28, in29, in30, in31, gs, en_out
  assign bit_extender_1_out = {{3{1'b0}}, priority_encoder_1_out};  // Bit_Extender bit_extender_1
  ROM rom_1 (.addr(bit_extender_1_out), .data(out_27));  // open: sel

  // Other names for the same wires on the sheet: A = in_1; B = in_2; C = in_3; D = in_4; E = in_5; F = in_6; G = in_7;
  //   H = in_8; I = in_9; J = in_10; K = in_11; L = in_12; M = in_13; N = in_14; O = in_15; P = in_16; Q = in_17;
  //   R = in_18; S = in_19; T = in_20; U = in_21; V = in_22; W = in_23; X = in_24; Y = in_25; Z = in_26

  // Notes on the sheet:
  //   contents of rom_1 (hex, n*v repeats v):
  //   1 2 3 4 5 6 7 8 9 a b c d f 10 11 12 13 14 15 16 17 18 19 1a 1b 1c 1d 1e 1f 20 21 22 23 24 25 26 27
endmodule
