// Logisim project RAM BUILDERS.circ as structural Verilog: 5 circuits, main circuit main
module main (
  input  [3:0] DATA,
  input  [3:0] DATA_2,
  input  INPUT__YES_NO,
  input  INPUT__YES_NO_2,
  input  [1:0] ADDRESS,
  output [3:0] OUTPUT,
  output [3:0] OUTPUT_2
);

  _4BIT_RAM u_4bit_ram_1 (.in_1(DATA), .in_2(INPUT__YES_NO), .in_3(ADDRESS), .out_4(OUTPUT));
  _4BIT_ALTERRAM u_4bit_alterram_1 (.in_1(DATA_2), .in_2(INPUT__YES_NO_2), .out_3(OUTPUT_2));

  // Notes on the sheet:
  //   4 BIT DATA with 2 BIT ADDRESSES RAM MODULE with Plexers
  //   Change a register essentially 1 bit ram
endmodule

module _4BIT_ALTERRAM (
  input  [3:0] in_1,
  input  in_2,
  output [3:0] out_3
);

  wire clock_1_out;
  wire [3:0] controlled_buffer_1_out;

  assign controlled_buffer_1_out = in_2 ? in_1 : 4'bz;  // Controlled_Buffer controlled_buffer_1
  Clock clock_1 (.out(clock_1_out));
  Register #(.width(4)) register_1 (.D(controlled_buffer_1_out), .Q(out_3), .clk(clock_1_out));  // open: en, clr
endmodule

module _4BIT_RAM (
  input  [3:0] in_1,
  input  in_2,
  input  [1:0] in_3,
  output [3:0] out_4
);

  wire demultiplexer_1_out0, demultiplexer_1_out1, demultiplexer_1_out2, demultiplexer_1_out3;
  wire [3:0] demultiplexer_2_out0, demultiplexer_2_out1, demultiplexer_2_out2, demultiplexer_2_out3,
       n4bit_alterram_1_out_3, n4bit_alterram_2_out_3, n4bit_alterram_3_out_3, n4bit_alterram_4_out_3;

  Demultiplexer #(.select(2)) demultiplexer_1 (
    .out0(demultiplexer_1_out0), .out1(demultiplexer_1_out1), .out2(demultiplexer_1_out2),
    .out3(demultiplexer_1_out3), .in(in_2), .sel(in_3));  // open: en
  Demultiplexer #(.select(2), .width(4)) demultiplexer_2 (
    .out0(demultiplexer_2_out0), .out1(demultiplexer_2_out1), .out2(demultiplexer_2_out2),
    .out3(demultiplexer_2_out3), .in(in_1), .sel(in_3));  // open: en
  _4BIT_ALTERRAM u_4bit_alterram_1 (
    .in_1(demultiplexer_2_out0), .in_2(demultiplexer_1_out0), .out_3(n4bit_alterram_1_out_3));
  _4BIT_ALTERRAM u_4bit_alterram_2 (
    .in_1(demultiplexer_2_out1), .in_2(demultiplexer_1_out1), .out_3(n4bit_alterram_2_out_3));
  _4BIT_ALTERRAM u_4bit_alterram_3 (
    .in_1(demultiplexer_2_out2), .in_2(demultiplexer_1_out2), .out_3(n4bit_alterram_3_out_3));
  _4BIT_ALTERRAM u_4bit_alterram_4 (
    .in_1(demultiplexer_2_out3), .in_2(demultiplexer_1_out3), .out_3(n4bit_alterram_4_out_3));
  Multiplexer #(.select(2), .width(4)) multiplexer_1 (
    .in0(n4bit_alterram_1_out_3), .in1(n4bit_alterram_2_out_3), .in2(n4bit_alterram_3_out_3),
    .in3(n4bit_alterram_4_out_3), .out(out_4), .sel(in_3));  // open: en
endmodule

module _4bit_ROM_w_o_plexers (
  input  [3:0] in_1,
  input  [3:0] in_2,
  input  [3:0] in_3,
  input  [3:0] in_4,
  input  [3:0] in_5,
  output [3:0] out_6
);

  wire comparator_1_eq, comparator_2_eq, comparator_3_eq, comparator_4_eq;
  wire [3:0] controlled_buffer_1_out, controlled_buffer_2_out, controlled_buffer_3_out,
       controlled_buffer_4_out;

  Comparator_part #(.width(4)) comparator_1 (.a(in_2), .b(4'b0000), .eq(comparator_1_eq));  // open: gt, lt
  Comparator_part #(.width(4)) comparator_2 (.a(in_2), .b(4'b0001), .eq(comparator_2_eq));  // open: gt, lt
  Comparator_part #(.width(4)) comparator_3 (.a(in_2), .b(4'b0010), .eq(comparator_3_eq));  // open: gt, lt
  Comparator_part #(.width(4)) comparator_4 (.a(in_2), .b(4'b0011), .eq(comparator_4_eq));  // open: gt, lt
  assign controlled_buffer_1_out = comparator_1_eq ? in_1 : 4'bz;  // Controlled_Buffer controlled_buffer_1
  assign out_6 = controlled_buffer_2_out;  // Buffer buffer_1, 4 bits wide
  assign controlled_buffer_2_out = comparator_2_eq ? in_3 : 4'bz;  // Controlled_Buffer controlled_buffer_2
  assign controlled_buffer_3_out = comparator_3_eq ? in_4 : 4'bz;  // Controlled_Buffer controlled_buffer_3
  assign controlled_buffer_4_out = comparator_4_eq ? in_5 : 4'bz;  // Controlled_Buffer controlled_buffer_4
  assign out_6 = controlled_buffer_1_out;  // Buffer buffer_2, 4 bits wide
  assign out_6 = controlled_buffer_3_out;  // Buffer buffer_3, 4 bits wide
  assign out_6 = controlled_buffer_4_out;  // Buffer buffer_4, 4 bits wide

  // Other names for the same wires on the sheet: A[3:0] = in_2
endmodule

module Comparator (
  input  [3:0] in_1,
  input  [3:0] in_2,
  output [3:0] out_3
);

  assign out_3 = in_1 & in_2;  // AND_Gate and_1, 4 bits wide
endmodule
