// Logisim project RAM EXPERIMENTS.circ as structural Verilog: 1 circuit, main circuit main
module main (
  input  [7:0] in_1,
  input  [7:0] in_2,
  input  [7:0] in_3,
  input  [7:0] in_4,
  input  in_5,
  input  in_6,
  input  [7:0] in_7,
  input  [7:0] in_8,
  input  in_9,
  output [7:0] OUTPUT,
  output [7:0] out_11,
  output [7:0] out_12
);

  wire clock_1_out, clock_2_out, not_1_out, not_2_out, not_3_out;

  Clock clock_1 (.out(clock_1_out));
  assign OUTPUT = in_5 ? in_1 : 8'bz;  // Controlled_Buffer controlled_buffer_1
  assign out_12 = in_9 ? in_7 : 8'bz;  // Controlled_Buffer controlled_buffer_2
  not not_1 (not_1_out, in_5);
  not not_2 (not_2_out, in_9);
  RAM ram_1 (.addr(in_2), .data(OUTPUT), .clk(clock_1_out), .ld(not_1_out));  // open: sel, clr
  RAM #(.bus("asynch")) ram_2 (.addr(in_8), .data(out_12), .ld(not_2_out));  // open: sel, clr
  Clock clock_2 (.out(clock_2_out));
  not not_3 (not_3_out, in_6);
  RAM #(.bus("separate")) ram_3 (
    .addr(in_3), .din(in_4), .data(out_11), .clk(clock_2_out), .ld(not_3_out));  // open: str, sel, clr

  // Notes on the sheet:
  //   Data
  //   ADDRESS
endmodule
