// Logisim project Logism Adders with 1 increments.circ as structural Verilog: 3 circuits, main circuit main
module main (
  input  in_1,
  input  in_2,
  input  in_3,
  input  in_4,
  input  in_5,
  input  in_6,
  input  in_7,
  input  in_8,
  input  in_9,
  input  in_10,
  input  Increment,
  input  A0,
  input  A1,
  input  A2,
  input  A3,
  output out_16,
  output out_17,
  output S0,
  output S1,
  output S2,
  output S3,
  output C_out
);

  wire half_adder_1_out_4, half_adder_2_out_4, half_adder_3_out_4;

  Half_Adder half_adder_1 (.in_1(Increment), .in_2(A0), .out_3(S0), .out_4(half_adder_1_out_4));
  Half_Adder half_adder_2 (.in_1(half_adder_1_out_4), .in_2(A1), .out_3(S1), .out_4(half_adder_2_out_4));
  Half_Adder half_adder_3 (.in_1(half_adder_2_out_4), .in_2(A2), .out_3(S2), .out_4(half_adder_3_out_4));
  Half_Adder half_adder_4 (.in_1(half_adder_3_out_4), .in_2(A3), .out_3(S3), .out_4(C_out));
  Half_Adder half_adder_5 (.in_1(in_4), .in_2(in_6), .out_3(out_16), .out_4(out_17));
  Full_Adder full_adder_1 (.in_1(in_1), .in_2(in_2));  // open: in_3, out_4, out_5
  Full_Adder full_adder_2 ();  // open: in_1, in_2, in_3, out_4, out_5
  Full_Adder full_adder_3 ();  // open: in_1, in_2, in_3, out_4, out_5
  Full_Adder full_adder_4 ();  // open: in_1, in_2, in_3, out_4, out_5
endmodule

module Half_Adder (
  input  in_1,
  input  in_2,
  output out_3,
  output out_4
);

  wire and_1_out, and_2_out, not_1_out, not_2_out;

  not not_1 (not_1_out, in_1);
  not not_2 (not_2_out, in_2);
  and and_1 (and_1_out, not_1_out, in_2);
  and and_2 (and_2_out, in_1, not_2_out);
  and and_3 (out_4, in_1, in_2);
  or or_1 (out_3, and_1_out, and_2_out);
endmodule

module Full_Adder (
  input  in_1,
  input  in_2,
  input  in_3,
  output out_4,
  output out_5
);

  wire half_adder_1_out_4, half_adder_2_out_3, half_adder_2_out_4;

  Half_Adder half_adder_1 (.in_1(in_1), .in_2(half_adder_2_out_3), .out_3(out_4), .out_4(half_adder_1_out_4));
  Half_Adder half_adder_2 (.in_1(in_2), .in_2(in_3), .out_3(half_adder_2_out_3), .out_4(half_adder_2_out_4));
  or or_1 (out_5, half_adder_1_out_4, half_adder_2_out_4);
endmodule
