// Logisim project Logism Adders.circ as structural Verilog: 3 circuits, main circuit main
module main (
  input  in_1,
  input  in_2,
  input  in_3,
  input  A,
  input  B,
  input  in_6,
  input  in_7,
  input  in_8,
  input  in_9,
  input  in_10,
  input  in_11,
  input  in_12,
  input  in_13,
  output out_14,
  output out_15,
  output Carry_Out,
  output out_17,
  output out_18,
  output out_19,
  output Sum
);

  wire and_1_out, and_2_out, full_addr_1_out_4, full_addr_1_out_5, half_adder_1_carry, half_adder_1_sum,
       half_adder_2_carry, xor_1_out;

  Full_ADDR full_addr_1 (
    .in_1(in_11), .in_2(in_12), .in_3(in_12), .out_4(full_addr_1_out_4), .out_5(full_addr_1_out_5));
  Half_Adder half_adder_1 (.A(in_1), .B(in_2), .Carry(half_adder_1_carry), .Sum(half_adder_1_sum));
  Half_Adder half_adder_2 (.A(half_adder_1_sum), .B(in_3), .Carry(half_adder_2_carry), .Sum(out_15));
  Full_ADDR full_addr_2 (.in_1(full_addr_1_out_4));  // open: in_2, in_3, out_4, out_5
  or or_1 (out_14, half_adder_1_carry, half_adder_2_carry);
  and and_1 (and_1_out, A, B);
  xor xor_1 (xor_1_out, A, B);
  and and_2 (and_2_out, xor_1_out, in_10);
  or or_2 (Carry_Out, and_1_out, and_2_out);
  xor xor_2 (Sum, in_10, xor_1_out);

  assign in_13 = in_12;
endmodule

module Half_Adder (
  input  A,
  input  B,
  output Carry,
  output Sum
);

  and and_1 (Carry, A, B);
  xor xor_1 (Sum, A, B);
endmodule

module Full_ADDR (
  input  in_1,
  input  in_2,
  input  in_3,
  output out_4,
  output out_5
);

  wire half_adder_1_carry, half_adder_1_sum, half_adder_2_carry;

  Half_Adder half_adder_1 (.A(in_1), .B(in_2), .Carry(half_adder_1_carry), .Sum(half_adder_1_sum));
  Half_Adder half_adder_2 (.A(half_adder_1_sum), .B(in_3), .Carry(half_adder_2_carry), .Sum(out_5));
  or or_1 (out_4, half_adder_1_carry, half_adder_2_carry);
endmodule
