// Logisim project Random.circ as structural Verilog: 1 circuit, main circuit main
module main (
  input  in_1,
  input  in_2,
  input  in_3,
  input  in_4,
  input  in_5,
  input  in_6,
  input  [7:0] in_7,
  input  in_8,
  input  in_9,
  input  in_10,
  input  in_11,
  input  in_12,
  input  in_13,
  input  in_14,
  input  in_15,
  input  in_16,
  input  in_17,
  input  in_18,
  input  in_19,
  input  in_20,
  output out_21,
  output out_22,
  output out_23,
  output out_24,
  output out_25,
  output out_26,
  output [7:0] out_27,
  output out_28,
  output out_29,
  output out_30,
  output out_31
);

  wire and_1_out, and_3_out, button_1_out, not_1_out, not_2_out, transistor_3_out, xor_1_out, xor_2_out,
       xor_3_out, xor_4_out;

  J_K_Flip_Flop j_k_ff_1 (
    .J(in_3), .K(in_4), .Q(out_22), .Qn(out_23), .preset(in_8), .en(in_9), .reset(in_6));  // open: clk
  not not_1 (not_1_out, in_15);
  not not_2 (not_2_out, in_16);
  xor xor_1 (xor_1_out, not_1_out, not_2_out);
  Transistor transistor_1 ();  // open: in, out, gate
  xor xor_2 (xor_2_out, not_1_out, xor_1_out);
  xor xor_3 (xor_3_out, xor_1_out, not_2_out);
  and and_1 (and_1_out, in_1, in_2);
  xor xor_4 (xor_4_out, in_1, in_2);
  xor xor_5 (out_28, in_13, in_14);
  nor nor_1 (out_29, xor_2_out, xor_3_out);
  Transistor #(.\type ("n")) transistor_2 (.in(in_18), .out(out_30), .gate(in_17));
  Transistor #(.\type ("n")) transistor_3 (.in(1'b1), .out(transistor_3_out), .gate(in_19));
  and and_2 (out_24, in_11, in_13, in_14);
  xor xor_6 (out_26, in_11, and_3_out);
  and and_3 (and_3_out, in_13, in_14);
  Transistor #(.\type ("n")) transistor_4 (.in(transistor_3_out), .out(out_31), .gate(in_20));
  // Probe on and_1_out
  // Probe on xor_4_out
  Counter counter_1 (.load(in_5), .D(in_7), .count(in_10), .Q(out_27), .carry(out_25), .clk(in_12));  // open: clr
  Button button_1 (.out(button_1_out));
  T_Flip_Flop t_ff_1 (.clk(button_1_out), .T(button_1_out), .Q(out_21));  // open: Qn, preset, reset, en

  // Notes on the sheet:
  //   AND Gate
  //   Half-Adder
  //   AND Gate with N Type Transistor
  //   Another AND Gate with N Type Transistors
  //   Two bit add one
endmodule
