// Logisim project September 23rd.circ as structural Verilog
module half_adder (
  input  A,
  input  B,
  output C_out,
  output Sum
);

  and and_1 (C_out, A, B);
  xor xor_1 (Sum, B, A);
endmodule

module Full_adder (
  input  A,
  input  B,
  input  C_in,
  output C_out,
  output Sum
);

  wire half_adder_1_c_out, half_adder_1_sum, half_adder_2_c_out;

  half_adder half_adder_1 (.A(A), .B(B), .C_out(half_adder_1_c_out), .Sum(half_adder_1_sum));
  half_adder half_adder_2 (.A(half_adder_1_sum), .B(C_in), .C_out(half_adder_2_c_out), .Sum(Sum));
  or or_1 (C_out, half_adder_1_c_out, half_adder_2_c_out);
endmodule

module _4_bit_adder (
  input  C_in,
  input  Q0,
  input  P0,
  input  Q1,
  input  P1,
  input  Q2,
  input  P2,
  input  Q3,
  input  P3,
  output out_10,
  output S1,
  output out_12,
  output out_13,
  output CO
);

  wire full_adder_1_c_out, full_adder_2_c_out, full_adder_3_c_out;

  Full_adder full_adder_1 (.A(P0), .B(Q0), .C_in(C_in), .C_out(full_adder_1_c_out), .Sum(out_10));
  Full_adder full_adder_2 (.A(P1), .B(Q1), .C_in(full_adder_1_c_out), .C_out(full_adder_2_c_out), .Sum(S1));
  Full_adder full_adder_3 (.A(P2), .B(Q2), .C_in(full_adder_2_c_out), .C_out(full_adder_3_c_out), .Sum(out_12));
  Full_adder full_adder_4 (.A(P3), .B(Q3), .C_in(full_adder_3_c_out), .C_out(CO), .Sum(out_13));

  // Notes on the sheet:
  //   S0
  //   S2
  //   S3
endmodule

module _4_bit_number__1 (
  input  Inc,
  input  A0,
  input  A1,
  input  A2,
  input  in_5,
  output X0,
  output X1,
  output X2,
  output X3,
  output X4
);

  wire half_adder_1_c_out, half_adder_2_c_out, half_adder_3_c_out;

  half_adder half_adder_1 (.A(Inc), .B(A0), .C_out(half_adder_1_c_out), .Sum(X0));
  half_adder half_adder_2 (.A(half_adder_1_c_out), .B(A1), .C_out(half_adder_2_c_out), .Sum(X1));
  half_adder half_adder_3 (.A(half_adder_2_c_out), .B(A2), .C_out(half_adder_3_c_out), .Sum(X2));
  half_adder half_adder_4 (.A(half_adder_3_c_out), .B(in_5), .C_out(X3), .Sum(X4));

  // Notes on the sheet:
  //   A3
endmodule

module half_Subtractor (
  input  A,
  input  in_2,
  output Sum,
  output Carry
);

  wire not_1_out;

  not not_1 (not_1_out, A);
  xor xor_1 (Sum, A, in_2);
  and and_1 (Carry, in_2, not_1_out);

  // Notes on the sheet:
  //   B
endmodule

module _4_bit_subtractor (
  input  G0,
  input  G2,
  input  G3,
  input  G1,
  input  P0,
  input  P1,
  input  P2,
  input  P3,
  output Integer_Overfow,
  output out_10,
  output S1,
  output out_12,
  output out_13
);

  wire full_adder_1_c_out, full_adder_2_c_out, full_adder_3_c_out, xor_1_out, xor_2_out, xor_3_out, xor_4_out;

  xor xor_1 (xor_1_out, P0, 1'b1);
  xor xor_2 (xor_2_out, P1, 1'b1);
  Full_adder full_adder_1 (.A(G0), .B(xor_1_out), .C_in(1'b1), .C_out(full_adder_1_c_out), .Sum(out_10));
  Full_adder full_adder_2 (.A(G1), .B(xor_2_out), .C_in(full_adder_1_c_out), .C_out(full_adder_2_c_out), .Sum(S1));
  xor xor_3 (xor_3_out, P2, 1'b1);
  xor xor_4 (xor_4_out, P3, 1'b1);
  Full_adder full_adder_3 (.A(G2), .B(xor_3_out), .C_in(full_adder_2_c_out), .C_out(full_adder_3_c_out), .Sum(out_12));
  Full_adder full_adder_4 (.A(G3), .B(xor_4_out), .C_in(full_adder_3_c_out), .C_out(Integer_Overfow), .Sum(out_13));

  // Notes on the sheet:
  //   S0
  //   S2
  //   G-P=S
  //   S3
endmodule

module _4_bit_adder_subtractor (
  input  G0,
  input  G2,
  input  G3,
  input  G1,
  input  P0,
  input  P1,
  input  P2,
  input  P3,
  input  in_9,
  output out_10,
  output out_11,
  output S1,
  output out_13,
  output out_14
);

  wire full_adder_1_c_out, full_adder_2_c_out, full_adder_3_c_out, xor_1_out, xor_2_out, xor_3_out, xor_4_out;

  xor xor_1 (xor_1_out, P0, in_9);
  Full_adder full_adder_1 (.A(G0), .B(xor_1_out), .C_in(in_9), .C_out(full_adder_1_c_out), .Sum(out_11));
  xor xor_2 (xor_2_out, P1, in_9);
  xor xor_3 (xor_3_out, P2, in_9);
  Full_adder full_adder_2 (.A(G1), .B(xor_2_out), .C_in(full_adder_1_c_out), .C_out(full_adder_2_c_out), .Sum(S1));
  Full_adder full_adder_3 (.A(G2), .B(xor_3_out), .C_in(full_adder_2_c_out), .C_out(full_adder_3_c_out), .Sum(out_13));
  xor xor_4 (xor_4_out, P3, in_9);
  Full_adder full_adder_4 (.A(G3), .B(xor_4_out), .C_in(full_adder_3_c_out), .C_out(out_10), .Sum(out_14));

  // Notes on the sheet:
  //   Adder = 0
  //   Subtractor = 1
  //   S0
  //   S2
  //   G-P=S
  //   S3
  //   DISREGARD Integer Overflow
endmodule
