// Logisim project logisim Circuit.circ as structural Verilog
module main (
  input  A,
  input  in_2,
  input  in_3,
  input  B,
  input  in_5,
  input  in_6,
  input  in_7,
  input  in_8,
  input  in_9,
  input  in_10,
  input  in_11,
  input  in_12,
  input  A_2,
  input  in_14,
  input  in_15,
  input  in_16,
  input  B_2,
  input  in_18,
  input  in_19,
  input  in_20,
  input  in_21,
  input  in_22,
  input  Carry_In,
  input  in_24,
  input  in_25,
  input  in_26,
  output Carry,
  output out_28,
  output Sum,
  output out_30,
  output out_31,
  output out_32,
  output Carry_Out,
  output out_34,
  output out_35,
  output Sum_2,
  output out_37,
  output out_38
);

  wire and_2_out, and_4_out, button_1_out, button_2_out, button_3_out, button_4_out, counter_1_carry,
       not_2_out, t_ff_1_q, t_ff_1_qn, xor_3_out;

  Button button_1 (.out(button_1_out));
  or OR (out_28, in_2, in_5);
  and AND (out_30, in_7, in_9);
  not NOT (out_31, in_11);
  nand NAND (out_32, in_14, in_16);
  nor NOR (out_34, in_19, in_21);
  xor XOR (out_35, in_22, in_24);
  xnor XNOR (out_37, in_25, in_26);
  Button button_2 (.out(button_2_out));
  Button button_3 (.out(button_3_out));
  Button button_4 (.out(button_4_out));
  Counter #(.max('h3), .ongoal("stay")) counter_1 (
    .count(button_2_out), .carry(counter_1_carry), .clk(button_2_out), .clr(button_3_out));  // open: load, D, Q
  T_Flip_Flop t_ff_1 (.clk(button_4_out), .T(button_4_out), .Q(t_ff_1_q), .Qn(t_ff_1_qn));  // open: preset, reset, en
  LED led_1 (.in(t_ff_1_qn));
  not not_2 (not_2_out, button_1_out);
  LED led_2 (.in(counter_1_carry));
  LED led_3 (.in(t_ff_1_q));
  LED led_4 (.in(not_2_out));
  LED led_5 (.in(button_1_out));
  _7_Segment_Display u_7_segment_display_1 (
    .g(in_10), .f(in_8), .a(in_6), .b(in_3), .e(in_12), .d(in_15), .c(in_18), .dp(in_20));
  and and_2 (and_2_out, A_2, B_2);
  and and_3 (Carry, A, B);
  xor xor_2 (Sum, A, B);
  xor xor_3 (xor_3_out, A_2, B_2);
  and and_4 (and_4_out, xor_3_out, Carry_In);
  or or_2 (Carry_Out, and_2_out, and_4_out);
  xor xor_4 (Sum_2, Carry_In, xor_3_out);

  assign out_38 = 1'b1;

  // Notes on the sheet:
  //   T-Flip Flop Without Storing Values
  //   Constant
  //   Counter
  //   Reset
  //   T-Flip Flop
  //   Basic Logic Gates
  //   Hex Digit Display
  //   Addition with one bit
endmodule
