// Logisim project hex 7 seg.circ as structural Verilog: 9 circuits, main circuit main
module main (
  input  in_1,
  input  in_2,
  input  in_3,
  input  in_4,
  input  [3:0] in_5
);

  wire a_1_x, b_1_x, c_1_x, d_1_x, e_1_x, f_1_x, g_1_x, output_1_a2, output_1_b2, output_1_c2, output_1_d2,
       output_1_e2, output_1_f2, output_1_g2;

  \output  output_1 (
    .A(in_5[3]), .B(in_5[2]), .C(in_5[1]), .D(in_5[0]), .A2(output_1_a2), .B2(output_1_b2), .C2(output_1_c2),
    .D2(output_1_d2), .E2(output_1_e2), .F2(output_1_f2), .G2(output_1_g2));
  A a_1 (.A(in_1), .B(in_2), .C(in_3), .D(in_4), .x(a_1_x));
  B b_1 (.A(in_1), .B(in_2), .C(in_3), .D(in_4), .x(b_1_x));
  C c_1 (.A(in_1), .B(in_2), .C(in_3), .D(in_4), .x(c_1_x));
  D d_1 (.A(in_1), .B(in_2), .C(in_3), .D(in_4), .x(d_1_x));
  E e_1 (.A(in_1), .B(in_2), .C(in_3), .D(in_4), .x(e_1_x));
  F f_1 (.A(in_1), .B(in_2), .C(in_3), .D(in_4), .x(f_1_x));
  G g_1 (.A(in_1), .B(in_2), .C(in_3), .D(in_4), .x(g_1_x));
  _7_Segment_Display u_7_segment_display_1 (
    .g(g_1_x), .f(f_1_x), .a(a_1_x), .b(b_1_x), .e(e_1_x), .d(d_1_x), .c(c_1_x));  // open: dp
  _7_Segment_Display u_7_segment_display_2 (
    .g(output_1_g2), .f(output_1_f2), .a(output_1_a2), .b(output_1_b2), .e(output_1_e2), .d(output_1_d2),
    .c(output_1_c2));  // open: dp
endmodule

module A (
  input  A,
  input  B,
  input  C,
  input  D,
  output x
);

  wire and_1_out, and_2_out, and_3_out, and_4_out, and_5_out, and_6_out, and_7_out, not_1_out, not_2_out,
       not_3_out, not_4_out, not_5_out, not_6_out, not_7_out, not_8_out, not_9_out;

  and and_1 (and_1_out, C, not_1_out);
  not not_1 (not_1_out, D);
  not not_2 (not_2_out, A);
  and and_2 (and_2_out, not_2_out, C);
  and and_3 (and_3_out, B, C);
  and and_4 (and_4_out, A, not_3_out);
  not not_3 (not_3_out, D);
  not not_4 (not_4_out, A);
  and and_5 (and_5_out, not_4_out, B, D);
  not not_5 (not_5_out, A);
  and and_6 (and_6_out, not_5_out, not_6_out, not_7_out);
  not not_6 (not_6_out, B);
  not not_7 (not_7_out, D);
  not not_8 (not_8_out, B);
  and and_7 (and_7_out, A, not_8_out, not_9_out);
  not not_9 (not_9_out, C);
  or or_1 (x, and_1_out, and_2_out, and_3_out, and_4_out, and_5_out, and_6_out, and_7_out);
endmodule

module B (
  input  A,
  input  B,
  input  C,
  input  D,
  output x
);

  wire and_1_out, and_2_out, and_3_out, and_4_out, and_5_out, and_6_out, not_1_out, not_2_out, not_3_out,
       not_4_out, not_5_out, not_6_out, not_7_out, not_8_out, not_9_out, not_10_out, not_11_out;

  not not_1 (not_1_out, A);
  and and_1 (and_1_out, not_1_out, not_2_out);
  not not_2 (not_2_out, B);
  not not_3 (not_3_out, B);
  and and_2 (and_2_out, not_3_out, not_4_out);
  not not_4 (not_4_out, C);
  not not_5 (not_5_out, A);
  and and_3 (and_3_out, not_5_out, C, D);
  not not_6 (not_6_out, A);
  not not_7 (not_7_out, C);
  and and_4 (and_4_out, not_6_out, not_7_out, not_8_out);
  not not_8 (not_8_out, D);
  not not_9 (not_9_out, C);
  and and_5 (and_5_out, A, not_9_out, D);
  and and_6 (and_6_out, A, not_10_out, not_11_out);
  not not_10 (not_10_out, B);
  not not_11 (not_11_out, D);
  or or_1 (x, and_1_out, and_2_out, and_3_out, and_4_out, and_5_out, and_6_out);
endmodule

module C (
  input  A,
  input  B,
  input  C,
  input  D,
  output x
);

  wire and_1_out, and_2_out, and_3_out, and_4_out, and_5_out, not_1_out, not_2_out, not_3_out, not_4_out,
       not_5_out, not_6_out;

  not not_1 (not_1_out, A);
  and and_1 (and_1_out, not_1_out, not_2_out);
  not not_2 (not_2_out, C);
  not not_3 (not_3_out, A);
  and and_2 (and_2_out, not_3_out, D);
  not not_4 (not_4_out, C);
  and and_3 (and_3_out, not_4_out, D);
  and and_4 (and_4_out, A, not_5_out);
  not not_5 (not_5_out, B);
  not not_6 (not_6_out, A);
  and and_5 (and_5_out, not_6_out, B);
  or or_1 (x, and_1_out, and_2_out, and_3_out, and_4_out, and_5_out);
endmodule

module D (
  input  A,
  input  B,
  input  C,
  input  D,
  output x
);

  wire and_1_out, and_2_out, and_3_out, and_4_out, and_5_out, and_6_out, not_1_out, not_2_out, not_3_out,
       not_4_out, not_5_out, not_6_out, not_7_out, not_8_out, not_9_out, not_10_out;

  not not_1 (not_1_out, B);
  and and_1 (and_1_out, not_1_out, C, D);
  not not_2 (not_2_out, A);
  and and_2 (and_2_out, not_2_out, C, not_3_out);
  not not_3 (not_3_out, D);
  and and_3 (and_3_out, B, C, not_4_out);
  not not_4 (not_4_out, D);
  and and_4 (and_4_out, B, not_5_out, D);
  not not_5 (not_5_out, C);
  not not_6 (not_6_out, B);
  and and_5 (and_5_out, not_6_out, not_7_out, not_8_out);
  not not_7 (not_7_out, C);
  not not_8 (not_8_out, D);
  and and_6 (and_6_out, A, not_9_out, not_10_out);
  not not_9 (not_9_out, C);
  not not_10 (not_10_out, D);
  or or_1 (x, and_1_out, and_2_out, and_3_out, and_4_out, and_5_out, and_6_out);
endmodule

module E (
  input  A,
  input  B,
  input  C,
  input  D,
  output x
);

  wire and_1_out, and_2_out, and_3_out, and_4_out, not_1_out, not_2_out, not_3_out, not_4_out;

  and and_1 (and_1_out, C, not_1_out);
  not not_1 (not_1_out, D);
  and and_2 (and_2_out, A, B);
  not not_2 (not_2_out, B);
  not not_3 (not_3_out, C);
  and and_3 (and_3_out, not_2_out, not_3_out, not_4_out);
  not not_4 (not_4_out, D);
  and and_4 (and_4_out, A, C);
  or or_1 (x, and_1_out, and_2_out, and_3_out, and_4_out);
endmodule

module F (
  input  A,
  input  B,
  input  C,
  input  D,
  output x
);

  wire and_1_out, and_2_out, and_3_out, and_4_out, and_5_out, not_1_out, not_2_out, not_3_out, not_4_out,
       not_5_out, not_6_out;

  not not_1 (not_1_out, C);
  and and_1 (and_1_out, not_1_out, not_2_out);
  not not_2 (not_2_out, D);
  and and_2 (and_2_out, A, not_3_out);
  not not_3 (not_3_out, B);
  and and_3 (and_3_out, A, C);
  and and_4 (and_4_out, B, not_4_out);
  not not_4 (not_4_out, D);
  not not_5 (not_5_out, A);
  and and_5 (and_5_out, not_5_out, B, not_6_out);
  not not_6 (not_6_out, C);
  or or_1 (x, and_1_out, and_2_out, and_3_out, and_4_out, and_5_out);
endmodule

module G (
  input  A,
  input  B,
  input  C,
  input  D,
  output x
);

  wire and_1_out, and_2_out, and_3_out, and_4_out, and_5_out, and_6_out, not_1_out, not_2_out, not_3_out,
       not_4_out, not_5_out;

  and and_1 (and_1_out, A, not_1_out);
  not not_1 (not_1_out, B);
  and and_2 (and_2_out, C, not_2_out);
  not not_2 (not_2_out, D);
  and and_3 (and_3_out, A, C);
  and and_4 (and_4_out, A, D);
  not not_3 (not_3_out, B);
  and and_5 (and_5_out, not_3_out, C);
  not not_4 (not_4_out, A);
  and and_6 (and_6_out, not_4_out, B, not_5_out);
  not not_5 (not_5_out, C);
  or or_1 (x, and_1_out, and_2_out, and_3_out, and_4_out, and_5_out, and_6_out);
endmodule

module \output  (
  input  A,
  input  B,
  input  C,
  input  D,
  output A2,
  output B2,
  output C2,
  output D2,
  output E2,
  output F2,
  output G2
);

  wire and_1_out, and_2_out, and_3_out, and_4_out, and_5_out, and_6_out, and_7_out, and_8_out, and_9_out,
       and_10_out, and_11_out, and_12_out, and_13_out, and_14_out, and_15_out, and_16_out, and_17_out,
       and_18_out, and_19_out, and_20_out, and_21_out, and_22_out, and_23_out, and_24_out, and_25_out,
       and_26_out, and_27_out, and_28_out, and_29_out, and_30_out, and_31_out, and_32_out, and_33_out,
       and_34_out, and_35_out, and_36_out, and_37_out, and_38_out, and_39_out, not_1_out, not_2_out,
       not_3_out, not_4_out, not_5_out, not_6_out, not_7_out, not_8_out, not_9_out, not_10_out, not_11_out,
       not_12_out, not_13_out, not_14_out, not_15_out, not_16_out, not_17_out, not_18_out, not_19_out,
       not_20_out, not_21_out, not_22_out, not_23_out, not_24_out, not_25_out, not_26_out, not_27_out,
       not_28_out, not_29_out, not_30_out, not_31_out, not_32_out, not_33_out, not_34_out, not_35_out,
       not_36_out, not_37_out, not_38_out, not_39_out, not_40_out, not_41_out, not_42_out, not_43_out,
       not_44_out, not_45_out, not_46_out, not_47_out, not_48_out, not_49_out, not_50_out, not_51_out;

  and and_1 (and_1_out, C, not_1_out);
  not not_1 (not_1_out, D);
  not not_2 (not_2_out, A);
  and and_2 (and_2_out, not_2_out, C);
  and and_3 (and_3_out, B, C);
  and and_4 (and_4_out, A, not_3_out);
  not not_3 (not_3_out, D);
  not not_4 (not_4_out, A);
  and and_5 (and_5_out, not_4_out, B, D);
  not not_5 (not_5_out, A);
  and and_6 (and_6_out, not_5_out, not_6_out, not_7_out);
  not not_6 (not_6_out, B);
  not not_7 (not_7_out, D);
  not not_8 (not_8_out, B);
  and and_7 (and_7_out, A, not_8_out, not_9_out);
  not not_9 (not_9_out, C);
  not not_10 (not_10_out, A);
  and and_8 (and_8_out, not_10_out, not_11_out);
  not not_11 (not_11_out, B);
  not not_12 (not_12_out, B);
  and and_9 (and_9_out, not_12_out, not_13_out);
  not not_13 (not_13_out, C);
  not not_14 (not_14_out, A);
  and and_10 (and_10_out, not_14_out, C, D);
  not not_15 (not_15_out, A);
  and and_11 (and_11_out, not_15_out, not_16_out, not_17_out);
  not not_16 (not_16_out, C);
  not not_17 (not_17_out, D);
  and and_12 (and_12_out, A, not_18_out, D);
  not not_18 (not_18_out, C);
  and and_13 (and_13_out, A, not_19_out, not_20_out);
  not not_19 (not_19_out, B);
  not not_20 (not_20_out, D);
  not not_21 (not_21_out, A);
  and and_14 (and_14_out, not_21_out, not_22_out);
  not not_22 (not_22_out, C);
  not not_23 (not_23_out, A);
  and and_15 (and_15_out, not_23_out, D);
  not not_24 (not_24_out, C);
  and and_16 (and_16_out, not_24_out, D);
  and and_17 (and_17_out, A, not_25_out);
  not not_25 (not_25_out, B);
  not not_26 (not_26_out, A);
  and and_18 (and_18_out, not_26_out, B);
  not not_27 (not_27_out, B);
  and and_19 (and_19_out, not_27_out, C, D);
  not not_28 (not_28_out, A);
  and and_20 (and_20_out, not_28_out, C, not_29_out);
  not not_29 (not_29_out, D);
  and and_21 (and_21_out, B, C, not_30_out);
  not not_30 (not_30_out, D);
  not not_31 (not_31_out, C);
  and and_22 (and_22_out, B, not_31_out, D);
  not not_32 (not_32_out, B);
  and and_23 (and_23_out, not_32_out, not_33_out, not_34_out);
  not not_33 (not_33_out, C);
  not not_34 (not_34_out, D);
  and and_24 (and_24_out, A, not_35_out, not_36_out);
  not not_35 (not_35_out, C);
  not not_36 (not_36_out, D);
  and and_25 (and_25_out, C, not_37_out);
  not not_37 (not_37_out, D);
  and and_26 (and_26_out, A, B);
  not not_38 (not_38_out, B);
  not not_39 (not_39_out, C);
  and and_27 (and_27_out, not_38_out, not_39_out, not_40_out);
  not not_40 (not_40_out, D);
  and and_28 (and_28_out, A, C);
  not not_41 (not_41_out, C);
  and and_29 (and_29_out, not_41_out, not_42_out);
  not not_42 (not_42_out, D);
  and and_30 (and_30_out, A, not_43_out);
  not not_43 (not_43_out, B);
  and and_31 (and_31_out, A, C);
  and and_32 (and_32_out, B, not_44_out);
  not not_44 (not_44_out, D);
  not not_45 (not_45_out, A);
  and and_33 (and_33_out, not_45_out, B, not_46_out);
  not not_46 (not_46_out, C);
  and and_34 (and_34_out, A, not_47_out);
  not not_47 (not_47_out, B);
  and and_35 (and_35_out, C, not_48_out);
  not not_48 (not_48_out, D);
  and and_36 (and_36_out, A, C);
  and and_37 (and_37_out, A, D);
  not not_49 (not_49_out, B);
  and and_38 (and_38_out, not_49_out, C);
  not not_50 (not_50_out, A);
  and and_39 (and_39_out, not_50_out, B, not_51_out);
  not not_51 (not_51_out, C);
  or or_1 (C2, and_14_out, and_15_out, and_16_out, and_17_out, and_18_out);
  or or_2 (E2, and_25_out, and_26_out, and_27_out, and_28_out);
  or or_3 (F2, and_29_out, and_30_out, and_31_out, and_32_out, and_33_out);
  or or_4 (A2, and_1_out, and_2_out, and_3_out, and_4_out, and_5_out, and_6_out, and_7_out);
  or or_5 (B2, and_8_out, and_9_out, and_10_out, and_11_out, and_12_out, and_13_out);
  or or_6 (D2, and_19_out, and_20_out, and_21_out, and_22_out, and_23_out, and_24_out);
  or or_7 (G2, and_34_out, and_35_out, and_36_out, and_37_out, and_38_out, and_39_out);
endmodule
