// Logisim project Adders.circ as structural Verilog: 3 circuits, main circuit main
module main (
  input  [3:0] in_1,
  input  [3:0] in_2,
  output [3:0] out_3,
  output out_4
);

  wire n2_bit_adder_1_out_5, n2_bit_adder_2_out_5, n2_bit_adder_3_out_5;

  _2_Bit_Adder u_2_bit_adder_1 (
    .in_1(1'b0), .in_2(in_1[0]), .in_3(in_2[0]), .out_4(out_3[0]), .out_5(n2_bit_adder_1_out_5));
  _2_Bit_Adder u_2_bit_adder_2 (
    .in_1(n2_bit_adder_1_out_5), .in_2(in_1[1]), .in_3(in_2[1]), .out_4(out_3[1]),
    .out_5(n2_bit_adder_2_out_5));
  _2_Bit_Adder u_2_bit_adder_3 (
    .in_1(n2_bit_adder_2_out_5), .in_2(in_1[2]), .in_3(in_2[2]), .out_4(out_3[2]),
    .out_5(n2_bit_adder_3_out_5));
  _2_Bit_Adder u_2_bit_adder_4 (
    .in_1(n2_bit_adder_3_out_5), .in_2(in_1[3]), .in_3(in_2[3]), .out_4(out_3[3]), .out_5(out_4));

  // Notes on the sheet:
  //   4 Bit Adder
endmodule

module _2_Bit_Adder (
  input  in_1,
  input  in_2,
  input  in_3,
  output out_4,
  output out_5
);

  wire and_1_out, and_2_out, and_3_out, xor_1_out;

  xor xor_1 (xor_1_out, in_2, in_3);
  and and_1 (and_1_out, in_1, in_2);
  and and_2 (and_2_out, in_1, in_3);
  and and_3 (and_3_out, in_2, in_3);
  xor xor_2 (out_4, in_1, xor_1_out);
  or or_1 (out_5, and_1_out, and_2_out, and_3_out);

  // Notes on the sheet:
  //   Full Adder
endmodule

module two_bit (
  input  [1:0] in_1,
  input  [1:0] in_2,
  output [1:0] out_3,
  output out_4
);

  wire n2_bit_adder_1_out_5;

  _2_Bit_Adder u_2_bit_adder_1 (
    .in_1(1'b0), .in_2(in_1[0]), .in_3(in_2[0]), .out_4(out_3[0]), .out_5(n2_bit_adder_1_out_5));
  _2_Bit_Adder u_2_bit_adder_2 (
    .in_1(n2_bit_adder_1_out_5), .in_2(in_1[1]), .in_3(in_2[1]), .out_4(out_3[1]), .out_5(out_4));

  // Notes on the sheet:
  //   Two bit adder
endmodule
