// Logisim project assignment.circ as structural Verilog: 8 circuits, main circuit main
module main (
  input  in_1,
  input  in_2,
  input  in_3,
  input  in_4,
  input  in_5,
  input  Shift,
  input  in_7,
  input  x,
  output out_9,
  output out_10,
  output out_11,
  output out_12,
  output out_13,
  output out_14,
  output out_15,
  output out_16,
  output out_17
);

  wire n8_ands_1_out_10, n8_ands_1_out_11, n8_ands_1_out_12, n8_ands_1_out_13, n8_ands_1_out_14,
       n8_ands_1_out_15, n8_ands_1_out_16, n8_ands_1_out_17, n8_ands_2_out_10, n8_ands_2_out_11,
       n8_ands_2_out_14, n8_ands_2_out_15, register_1_out_6, register_1_out_7, register_1_out_8,
       register_1_out_9, register_1_out_10, register_1_out_11, register_1_out_12, register_1_out_13;

  Register register_1 (
    .in_1(in_1), .in_2(in_3), .in_3(in_4), .in_4(in_5), .in_5(in_5), .out_6(register_1_out_6),
    .out_7(register_1_out_7), .out_8(register_1_out_8), .out_9(register_1_out_9), .out_10(register_1_out_10),
    .out_11(register_1_out_11), .out_12(register_1_out_12), .out_13(register_1_out_13));
  _8_ands u_8_ands_1 (
    .in_1(register_1_out_6), .in_2(register_1_out_7), .in_3(register_1_out_8), .in_4(register_1_out_9),
    .in_5(register_1_out_10), .in_6(register_1_out_11), .in_7(register_1_out_12), .in_8(register_1_out_13),
    .in_9(in_7), .out_10(n8_ands_1_out_10), .out_11(n8_ands_1_out_11), .out_12(n8_ands_1_out_12),
    .out_13(n8_ands_1_out_13), .out_14(n8_ands_1_out_14), .out_15(n8_ands_1_out_15),
    .out_16(n8_ands_1_out_16), .out_17(n8_ands_1_out_17));
  _8_ands u_8_ands_2 (
    .in_1(register_1_out_6), .in_2(register_1_out_7), .in_3(register_1_out_8), .in_4(register_1_out_9),
    .in_5(register_1_out_10), .in_6(register_1_out_11), .in_7(register_1_out_12), .in_8(register_1_out_13),
    .in_9(x), .out_10(n8_ands_2_out_10), .out_11(n8_ands_2_out_11), .out_14(n8_ands_2_out_14),
    .out_15(n8_ands_2_out_15));  // open: out_12, out_13, out_16, out_17
  _2_by_2_multiplier u_2_by_2_multiplier_1 (
    .in_1(n8_ands_2_out_10), .in_2(n8_ands_2_out_11), .in_3(n8_ands_2_out_14), .in_4(n8_ands_2_out_15),
    .out_5(out_14), .out_6(out_15), .out_7(out_16), .out_8(out_17));
  _4_Bit_Adder u_4_bit_adder_1 (
    .in_1(in_2), .in_2(n8_ands_1_out_10), .in_3(n8_ands_1_out_11), .in_4(n8_ands_1_out_12),
    .in_5(n8_ands_1_out_13), .in_6(n8_ands_1_out_14), .in_7(n8_ands_1_out_15), .in_8(n8_ands_1_out_16),
    .in_9(n8_ands_1_out_17), .out_10(out_9), .out_11(out_10), .out_12(out_11), .out_13(out_12),
    .out_14(out_13));

  assign Shift = in_5;
endmodule

module FullAdder (
  input  A,
  input  B,
  input  C_out,
  output out_4,
  output out_5
);

  wire and_1_out, and_2_out, xor_1_out;

  xor xor_1 (xor_1_out, A, B);
  and and_1 (and_1_out, A, B);
  and and_2 (and_2_out, xor_1_out, C_out);
  or or_1 (out_4, and_1_out, and_2_out);
  xor xor_2 (out_5, xor_1_out, C_out);
endmodule

module _4_Bit_Adder (
  input  in_1,
  input  in_2,
  input  in_3,
  input  in_4,
  input  in_5,
  input  in_6,
  input  in_7,
  input  in_8,
  input  in_9,
  output out_10,
  output out_11,
  output out_12,
  output out_13,
  output out_14
);

  wire fulladder_2_out_4, fulladder_3_out_4, fulladder_4_out_4;

  FullAdder fulladder_1 (.A(in_5), .B(in_9), .C_out(fulladder_4_out_4), .out_4(out_14), .out_5(out_13));
  FullAdder fulladder_2 (.A(in_2), .B(in_6), .C_out(in_1), .out_4(fulladder_2_out_4), .out_5(out_10));
  FullAdder fulladder_3 (.A(in_3), .B(in_7), .C_out(fulladder_2_out_4), .out_4(fulladder_3_out_4), .out_5(out_11));
  FullAdder fulladder_4 (.A(in_4), .B(in_8), .C_out(fulladder_3_out_4), .out_4(fulladder_4_out_4), .out_5(out_12));
endmodule

module Store (
  input  in_1,
  input  in_2,
  input  in_3,
  input  in_4,
  input  in_5,
  output out_6,
  output out_7,
  output out_8,
  output out_9
);

  wire clock_1_out, not_1_out;

  Clock clock_1 (.out(clock_1_out));
  not not_1 (not_1_out, in_5);
  D_Flip_Flop d_ff_1 (.clk(clock_1_out), .D(in_1), .Q(out_6), .en(not_1_out));  // open: Qn, preset, reset
  D_Flip_Flop d_ff_2 (.clk(clock_1_out), .D(in_2), .Q(out_7), .en(not_1_out));  // open: Qn, preset, reset
  D_Flip_Flop d_ff_3 (.clk(clock_1_out), .D(in_3), .Q(out_8), .en(not_1_out));  // open: Qn, preset, reset
  D_Flip_Flop d_ff_4 (.clk(clock_1_out), .D(in_4), .Q(out_9), .en(not_1_out));  // open: Qn, preset, reset
endmodule

module Register (
  input  in_1,
  input  in_2,
  input  in_3,
  input  in_4,
  input  in_5,
  output out_6,
  output out_7,
  output out_8,
  output out_9,
  output out_10,
  output out_11,
  output out_12,
  output out_13
);

  and and_1 (out_11, in_5, in_2);
  and and_2 (out_12, in_5, in_3);
  and and_3 (out_13, in_4, in_5);
  Store store_1 (
    .in_1(in_1), .in_2(in_2), .in_3(in_3), .in_4(in_4), .in_5(in_5), .out_6(out_6), .out_7(out_7),
    .out_8(out_8), .out_9(out_9));
  and and_4 (out_10, in_5, in_1);
endmodule

module _8_ands (
  input  in_1,
  input  in_2,
  input  in_3,
  input  in_4,
  input  in_5,
  input  in_6,
  input  in_7,
  input  in_8,
  input  in_9,
  output out_10,
  output out_11,
  output out_12,
  output out_13,
  output out_14,
  output out_15,
  output out_16,
  output out_17
);

  and and_1 (out_10, in_1, in_9);
  and and_2 (out_11, in_2, in_9);
  and and_3 (out_12, in_3, in_9);
  and and_4 (out_13, in_4, in_9);
  and and_5 (out_14, in_5, in_9);
  and and_6 (out_15, in_6, in_9);
  and and_7 (out_16, in_7, in_9);
  and and_8 (out_17, in_8, in_9);
endmodule

module _2_by_2_multiplier (
  input  in_1,
  input  in_2,
  input  in_3,
  input  in_4,
  output out_5,
  output out_6,
  output out_7,
  output out_8
);

  wire and_1_out, and_3_out, and_4_out, and_5_out;

  and and_1 (and_1_out, in_1, in_4);
  and and_2 (out_5, in_1, in_3);
  and and_3 (and_3_out, in_2, in_3);
  and and_4 (and_4_out, in_2, in_4);
  xor xor_1 (out_6, and_1_out, and_3_out);
  and and_5 (and_5_out, and_1_out, and_3_out);
  and and_6 (out_8, and_5_out, and_4_out);
  xor xor_2 (out_7, and_5_out, and_4_out);
endmodule

module Full_Circuit_Messy (
  input  I0,
  input  I1,
  input  I2,
  input  I3,
  input  Shift,
  input  Add,
  input  Multiply,
  output O0,
  output O1,
  output O2,
  output O3,
  output O4
);

  wire and_1_out, and_2_out, and_3_out, and_4_out, and_5_out, and_6_out, and_7_out, and_8_out, and_9_out,
       and_10_out, and_11_out, and_12_out, and_13_out, and_14_out, and_15_out, and_16_out, and_17_out,
       and_18_out, and_19_out, and_20_out, and_21_out, and_22_out, and_23_out, and_24_out, and_25_out,
       and_26_out, and_27_out, and_28_out, and_29_out, and_30_out, clock_1_out, d_ff_1_q, d_ff_2_q, d_ff_3_q,
       d_ff_4_q, not_1_out, or_1_out, or_2_out, or_3_out, xor_1_out, xor_2_out, xor_3_out, xor_4_out,
       xor_5_out, xor_6_out, xor_7_out, xor_8_out, xor_9_out, xor_10_out;

  and and_1 (and_1_out, I0, Shift);
  and and_2 (and_2_out, I1, Shift);
  Clock clock_1 (.out(clock_1_out));
  and and_3 (and_3_out, I2, Shift);
  and and_4 (and_4_out, I3, Shift);
  D_Flip_Flop d_ff_1 (.clk(clock_1_out), .D(I0), .Q(d_ff_1_q), .en(not_1_out));  // open: Qn, preset, reset
  D_Flip_Flop d_ff_2 (.clk(clock_1_out), .D(I1), .Q(d_ff_2_q), .en(not_1_out));  // open: Qn, preset, reset
  D_Flip_Flop d_ff_3 (.clk(clock_1_out), .D(I2), .Q(d_ff_3_q), .en(not_1_out));  // open: Qn, preset, reset
  D_Flip_Flop d_ff_4 (.clk(clock_1_out), .D(I3), .Q(d_ff_4_q), .en(not_1_out));  // open: Qn, preset, reset
  not not_1 (not_1_out, Shift);
  and and_5 (and_5_out, d_ff_1_q, Add);
  and and_6 (and_6_out, d_ff_2_q, Add);
  and and_7 (and_7_out, d_ff_3_q, Add);
  and and_8 (and_8_out, d_ff_4_q, Add);
  and and_9 (and_9_out, and_1_out, Add);
  and and_10 (and_10_out, and_2_out, Add);
  and and_11 (and_11_out, and_3_out, Add);
  and and_12 (and_12_out, and_4_out, Add);
  and and_13 (and_13_out, and_1_out, Multiply);
  and and_14 (and_14_out, and_2_out, Multiply);
  and and_15 (and_15_out, d_ff_1_q, Multiply);
  and and_16 (and_16_out, d_ff_2_q, Multiply);
  xor xor_1 (xor_1_out, and_5_out, and_9_out);
  and and_17 (and_17_out, and_5_out, and_9_out);
  and and_18 (and_18_out, xor_1_out, 1'b0);
  xor xor_2 (xor_2_out, and_6_out, and_10_out);
  and and_19 (and_19_out, and_6_out, and_10_out);
  xor xor_3 (xor_3_out, and_7_out, and_11_out);
  and and_20 (and_20_out, and_7_out, and_11_out);
  xor xor_4 (xor_4_out, and_8_out, and_12_out);
  and and_21 (and_21_out, and_8_out, and_12_out);
  and and_22 (and_22_out, and_13_out, and_16_out);
  and and_23 (and_23_out, and_13_out, and_15_out);
  and and_24 (and_24_out, and_14_out, and_15_out);
  and and_25 (and_25_out, and_14_out, and_16_out);
  xor xor_5 (xor_5_out, xor_1_out, 1'b0);
  or or_1 (or_1_out, and_18_out, and_17_out);
  and and_26 (and_26_out, xor_2_out, or_1_out);
  and and_27 (and_27_out, xor_3_out, or_2_out);
  and and_28 (and_28_out, xor_4_out, or_3_out);
  or or_2 (or_2_out, and_26_out, and_19_out);
  or or_3 (or_3_out, and_27_out, and_20_out);
  xor xor_6 (xor_6_out, xor_4_out, or_3_out);
  or or_4 (O4, and_28_out, and_21_out);
  xor xor_7 (xor_7_out, and_22_out, and_24_out);
  and and_29 (and_29_out, and_22_out, and_24_out);
  xor xor_8 (xor_8_out, xor_2_out, or_1_out);
  xor xor_9 (xor_9_out, xor_3_out, or_2_out);
  xor xor_10 (xor_10_out, and_29_out, and_25_out);
  and and_30 (and_30_out, and_29_out, and_25_out);
  or or_5 (O0, xor_5_out, and_23_out);
  or or_6 (O1, xor_8_out, xor_7_out);
  or or_7 (O2, xor_9_out, xor_10_out);
  or or_8 (O3, xor_6_out, and_30_out);

  // Notes on the sheet:
  //   For Addition
  //   2. Press +
  //   3. Press Shift
  //   1. Type in first number
  //   4. Type Second Number
  //   For Multiplication
  //   2. Press x and shift
  //   1. Type in First number use only A and B
  //   3. Type Second Number use A and B
endmodule
